// Logisim project logicProject.circ as structural Verilog
module Dividor (
  input  As,
  input  A1,
  input  A0,
  input  Bs,
  input  B1,
  input  B0,
  output F0,
  output Fz,
  output F1,
  output F_z,
  output Bl,
  output S
);

  wire and_3_out, and_4_out, and_5_out, and_6_out, n7448_1_p10, n7448_1_p11, n7448_1_p12, n7448_1_p13,
       n7448_1_p14, n7448_1_p15, n7448_1_p16, not_1_out, not_2_out, or_1_out, or_3_out, or_4_out, xor_1_out;

  not not_1 (not_1_out, B1);
  not not_2 (not_2_out, B0);
  and and_1 (F1, not_1_out, A1);
  and and_2 (F_z, not_1_out, not_2_out);
  or or_1 (or_1_out, not_1_out, A1);
  and and_3 (and_3_out, A1, B1);
  and and_4 (and_4_out, or_1_out, A0);
  and and_5 (and_5_out, and_3_out, not_2_out);
  xor xor_1 (xor_1_out, As, Bs);
  or or_2 (F0, and_4_out, and_5_out);
  LED led_1 (.in(F_z));
  xor xor_2 (Bl, F_z, 1'b1);
  or or_3 (or_3_out, F0, F1);
  // _7448 7448_1: pin names not known; wires that end beside it: F1, 1'b0, Bl, 1'b1, 1'b1, 1'b0, F0, 1'b0, 1'b1, n7448_1_p10, n7448_1_p11, n7448_1_p12, n7448_1_p13, n7448_1_p14, n7448_1_p15, n7448_1_p16
  or or_4 (or_4_out, or_3_out, F_z);
  and and_6 (and_6_out, Bl, xor_1_out);
  not not_3 (Fz, or_4_out);
  _7_Segment_Display u_7_segment_display_1 (.g(S));  // open: f, a, b, e, d, c, dp
  LED led_2 (.in(Fz));
  and and_7 (S, or_4_out, and_6_out);
  _7_Segment_Display u_7_segment_display_2 (
    .g(n7448_1_p11), .f(n7448_1_p10), .a(n7448_1_p12), .b(n7448_1_p13), .e(n7448_1_p16), .d(n7448_1_p15),
    .c(n7448_1_p14));  // open: dp

  // Notes on the sheet:
  //   Note1: the seven segment doesn't turn off, it gives 8 instead, when you apply LOW on BL pin (library problem)
  //   Note2: I use anode 7 segment and 7447 instead. (the standard library doesn't contain them.)
endmodule
